# Fritzing sketch Automatic Bell System circuit diagram (saved by Fritzing 0.9.2b)

parts:
  Part1 = Arduino Mega 2560 (Rev3)
  ZS-042_RTC1 = ZS-042 RTC Module
  Part2 = KY-019 5V Relay Module [package="Breakout board"]
  Display1 = LCD screen 16x2 IIC [part_number=101290]
  Part3 = 4x4 Keypad [part_number=101207]
  S2 = Square Pushbutton

nets:
  N1: Part1.D21/SCL, ZS-042_RTC1.SCL#9
  N2: Part1.D20/SDA, ZS-042_RTC1.SDA#8
  N3: Part1.GND, ZS-042_RTC1.GND#6, Part2.-, S2.leg0
  N4: Part1.RESET, S2.leg1
  N5: Part1.5V, ZS-042_RTC1.VCC#7, Part2.+
  N6: Part1.D22, Part3.1
  N7: Part1.D24, Part3.2
  N8: Part1.D26, Part3.3
  N9: Part1.D28, Part3.4
  N10: Part1.D30, Part3.5
  N11: Part1.D32, Part3.6
  N12: Part1.D34, Part3.7
  N13: Part1.D36, Part3.8
  N14: Part1.D38, Part2.S
  N15: ZS-042_RTC1.SDA#2, Display1.SDA
  N16: ZS-042_RTC1.SCL#3, Display1.SCL

notes:
  I2C 16x2 Display
  RTC DS3231
  4x4 Keypad
  Push Button
  5V Single channel relay

custom parts:
  KY-019 5V Relay Module: KY-019 5V Relay module, used to control AC circuits.
  LCD screen 16x2 IIC: LCD screen with HD44780 controller enables showing text, symbols, value or anything else that comes from Croduino/Arduino. It is capable of showing 16 symbols in two lines and therefore can be used in many projects that need to send clearly visible and legible output information.. • Color of symbols: White • Backlight: Blue • Dimensions: 80 x 36 x 12 mm • Screen dimensions: 64.5 x 16 mm •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
  4x4 Keypad: Matrix membrane keypad 4x4
